# Fritzing sketch oven_conveyor_diagram (saved by Fritzing 0.9.4)

parts:
  LCD1 = LCD screen
  Part1 = Arduino Uno (Rev3)
  RE1 = Rotary Encoder [package=THT]

nets:
  VSS: LCD1.VSS, Part1.GND, RE1.EncoderPinB
  VDD: LCD1.VDD, Part1.5V
  N1: LCD1.V0, Part1.D6_PWM
  N2: LCD1.RS, Part1.D12/MISO
  N3: LCD1.E, Part1.D11_PWM/MOSI
  N4: LCD1.DB4, Part1.D10_PWM/SS
  N5: LCD1.DB5, Part1.D9_PWM
  N6: LCD1.DB6, Part1.D8
  N7: LCD1.DB7, Part1.D7
  N8: Part1.D2, RE1.EncoderPinA
  N9: Part1.D3_PWM, RE1.EncoderPinC

notes:
  These run to stepper driver unit and provide motor control signals
